// Logisim project Controle Principal.circ as structural Verilog: 1 circuit, main circuit main
// Tipo R
module main (
  input  Op5,
  input  Op4,
  input  Op3,
  input  Op2,
  input  Op1,
  input  Op0,
  output RegDst,
  output AluSrc,
  output MemToReg,
  output RegWrite,
  output MemRead,
  output MemWrite,
  output Branch,
  output AluOp1,
  output AluOp0
);

  and Tipo_R (AluOp1, ~Op5, ~Op4, ~Op3, ~Op2, ~Op1, ~Op0);  // AND_Gate
  and lw (MemRead, Op5, ~Op4, ~Op3, ~Op2, Op1, Op0);  // AND_Gate
  and sw (MemWrite, Op5, ~Op4, Op3, ~Op2, Op1, Op0);  // AND_Gate
  and beq (AluOp0, ~Op5, ~Op4, ~Op3, Op2, ~Op1, ~Op0);  // AND_Gate
  or or_1 (AluSrc, MemWrite, MemRead);
  or or_2 (RegWrite, AluOp1, MemRead);

  assign Branch = AluOp0;
  assign MemToReg = MemRead;
  assign RegDst = AluOp1;
endmodule
