// Logisim project ULA 4 bits Controle.circ as structural Verilog: 1 circuit, main circuit main
// Operation0
module main (
  input  A0,
  input  Ainvert,
  input  B0,
  input  Bnegado,
  input  A1,
  input  B1,
  input  Less,
  input  A2,
  input  in_9,
  input  ALUop0,
  input  ALUop1,
  input  f3,
  input  f2,
  input  f1,
  input  f0,
  input  B2,
  input  Less_2,
  input  A3,
  input  B3,
  input  [1:0] Operation,
  input  Less_3,
  output R0,
  output R1,
  output Zero,
  output R2,
  output R3,
  output Ainvert_2,
  output Bnegado_2,
  output Operation1,
  output Operation0
);

  wire adder_1_cout, adder_1_out, adder_2_cout, adder_2_out, adder_3_cout, adder_3_out, adder_4_out,
       and_1_out, and_3_out, and_4_out, and_5_out, and_6_out, multiplexer_1_out, multiplexer_2_out,
       multiplexer_3_out, multiplexer_4_out, multiplexer_5_out, multiplexer_6_out, multiplexer_7_out,
       multiplexer_8_out, not_1_out, not_2_out, not_3_out, not_4_out, not_5_out, not_6_out, not_7_out,
       not_8_out, or_3_out, or_4_out, or_5_out, or_6_out, or_7_out;

  or or_1 (Bnegado_2, ALUop0, and_1_out);
  and and_1 (and_1_out, f1, ALUop1);
  or or_2 (Operation1, ~ALUop1, ~f2);  // OR_Gate
  or or_3 (or_3_out, f3, f0);
  and and_2 (Operation0, ALUop1, or_3_out);
  not not_1 (not_1_out, A0);
  not not_2 (not_2_out, B0);
  not not_3 (not_3_out, A1);
  not not_4 (not_4_out, B1);
  not not_5 (not_5_out, A2);
  not not_6 (not_6_out, B2);
  not not_7 (not_7_out, A3);
  not not_8 (not_8_out, B3);
  Multiplexer #(.enable("false")) multiplexer_1 (.in0(A0), .in1(not_1_out), .out(multiplexer_1_out), .sel(Ainvert));
  Multiplexer #(.enable("false")) multiplexer_2 (.in0(B0), .in1(not_2_out), .out(multiplexer_2_out), .sel(Bnegado));
  Multiplexer #(.enable("false")) multiplexer_3 (.in0(A1), .in1(not_3_out), .out(multiplexer_3_out), .sel(Ainvert));
  Multiplexer #(.enable("false")) multiplexer_4 (.in0(B1), .in1(not_4_out), .out(multiplexer_4_out), .sel(Bnegado));
  Multiplexer #(.enable("false")) multiplexer_5 (.in0(A2), .in1(not_5_out), .out(multiplexer_5_out), .sel(Ainvert));
  Multiplexer #(.enable("false")) multiplexer_6 (.in0(B2), .in1(not_6_out), .out(multiplexer_6_out), .sel(Bnegado));
  Multiplexer #(.enable("false")) multiplexer_7 (.in0(A3), .in1(not_7_out), .out(multiplexer_7_out), .sel(Ainvert));
  Multiplexer #(.enable("false")) multiplexer_8 (.in0(B3), .in1(not_8_out), .out(multiplexer_8_out), .sel(Bnegado));
  and and_3 (and_3_out, multiplexer_1_out, multiplexer_2_out);
  or or_4 (or_4_out, multiplexer_1_out, multiplexer_2_out);
  Adder #(.width(1)) adder_1 (
    .a(multiplexer_1_out), .b(multiplexer_2_out), .out(adder_1_out), .cin(Bnegado), .cout(adder_1_cout));
  and and_4 (and_4_out, multiplexer_3_out, multiplexer_4_out);
  or or_5 (or_5_out, multiplexer_3_out, multiplexer_4_out);
  Adder #(.width(1)) adder_2 (
    .a(multiplexer_3_out), .b(multiplexer_4_out), .out(adder_2_out), .cin(adder_1_cout), .cout(adder_2_cout));
  and and_5 (and_5_out, multiplexer_5_out, multiplexer_6_out);
  or or_6 (or_6_out, multiplexer_5_out, multiplexer_6_out);
  Adder #(.width(1)) adder_3 (
    .a(multiplexer_5_out), .b(multiplexer_6_out), .out(adder_3_out), .cin(adder_2_cout), .cout(adder_3_cout));
  and and_6 (and_6_out, multiplexer_7_out, multiplexer_8_out);
  or or_7 (or_7_out, multiplexer_7_out, multiplexer_8_out);
  Adder #(.width(1)) adder_4 (
    .a(multiplexer_7_out), .b(multiplexer_8_out), .out(adder_4_out), .cin(adder_3_cout));  // open: cout
  Multiplexer #(.select(2), .enable("false")) multiplexer_9 (
    .in0(and_3_out), .in1(or_4_out), .in2(adder_1_out), .in3(adder_4_out), .out(R0), .sel(Operation));
  Multiplexer #(.select(2), .enable("false")) multiplexer_10 (
    .in0(and_4_out), .in1(or_5_out), .in2(adder_2_out), .in3(Less), .out(R1), .sel(Operation));
  Multiplexer #(.select(2), .enable("false")) multiplexer_11 (
    .in0(and_5_out), .in1(or_6_out), .in2(adder_3_out), .in3(Less_2), .out(R2), .sel(Operation));
  Multiplexer #(.select(2), .enable("false")) multiplexer_12 (
    .in0(and_6_out), .in1(or_7_out), .in2(adder_4_out), .in3(Less_3), .out(R3), .sel(Operation));
  nor nor_1 (Zero, R0, R1, R2, R3);

  assign Ainvert_2 = in_9;
endmodule
