// Logisim project ula.circ as structural Verilog: 1 circuit, main circuit main
module main (
  input  in_1,
  input  in_2,
  input  in_3,
  input  in_4,
  input  in_5,
  input  in_6,
  input  in_7,
  input  in_8,
  input  in_9,
  input  in_10,
  input  in_11,
  input  in_12,
  input  [1:0] selecao,
  output out_14,
  output out_15,
  output out_16,
  output out_17,
  output out_18
);

  wire adder_1_out, adder_2_cout, adder_2_out, adder_3_cout, adder_3_out, adder_4_cout, adder_4_out,
       and_1_out, and_2_out, and_3_out, and_4_out, multiplexer_1_out, multiplexer_2_out, multiplexer_3_out,
       multiplexer_4_out, multiplexer_5_out, multiplexer_6_out, multiplexer_7_out, multiplexer_8_out,
       not_1_out, not_2_out, not_3_out, not_4_out, not_5_out, not_6_out, not_7_out, not_8_out, or_1_out,
       or_2_out, or_3_out, or_4_out;

  not not_1 (not_1_out, in_3);
  not not_2 (not_2_out, in_4);
  not not_3 (not_3_out, in_5);
  not not_4 (not_4_out, in_6);
  not not_5 (not_5_out, in_7);
  not not_6 (not_6_out, in_8);
  not not_7 (not_7_out, in_9);
  not not_8 (not_8_out, in_2);
  Multiplexer multiplexer_1 (.in0(in_3), .in1(not_1_out), .out(multiplexer_1_out), .sel(in_11));  // open: en
  Multiplexer multiplexer_2 (.in0(in_5), .in1(not_3_out), .out(multiplexer_2_out), .sel(in_11));  // open: en
  Multiplexer multiplexer_3 (.in0(in_7), .in1(not_5_out), .out(multiplexer_3_out), .sel(in_11));  // open: en
  Multiplexer multiplexer_4 (.in0(in_9), .in1(not_7_out), .out(multiplexer_4_out), .sel(in_11));  // open: en
  Multiplexer multiplexer_5 (.in0(in_2), .in1(not_8_out), .out(multiplexer_5_out), .sel(in_12));  // open: en
  Multiplexer multiplexer_6 (.in0(in_4), .in1(not_2_out), .out(multiplexer_6_out), .sel(in_12));  // open: en
  Multiplexer multiplexer_7 (.in0(in_6), .in1(not_4_out), .out(multiplexer_7_out), .sel(in_12));  // open: en
  Multiplexer multiplexer_8 (.in0(in_8), .in1(not_6_out), .out(multiplexer_8_out), .sel(in_12));  // open: en
  Adder #(.width(1)) adder_1 (
    .a(multiplexer_4_out), .b(multiplexer_8_out), .out(adder_1_out), .cin(adder_4_cout), .cout(out_18));
  Adder #(.width(1)) adder_2 (
    .a(multiplexer_1_out), .b(multiplexer_5_out), .out(adder_2_out), .cin(in_1), .cout(adder_2_cout));
  Adder #(.width(1)) adder_3 (
    .a(multiplexer_2_out), .b(multiplexer_6_out), .out(adder_3_out), .cin(adder_2_cout), .cout(adder_3_cout));
  Adder #(.width(1)) adder_4 (
    .a(multiplexer_3_out), .b(multiplexer_7_out), .out(adder_4_out), .cin(adder_3_cout), .cout(adder_4_cout));
  and and_1 (and_1_out, multiplexer_5_out, multiplexer_1_out);
  or or_1 (or_1_out, multiplexer_1_out, multiplexer_5_out);
  and and_2 (and_2_out, multiplexer_6_out, multiplexer_2_out);
  or or_2 (or_2_out, multiplexer_2_out, multiplexer_6_out);
  and and_3 (and_3_out, multiplexer_7_out, multiplexer_3_out);
  or or_3 (or_3_out, multiplexer_3_out, multiplexer_7_out);
  and and_4 (and_4_out, multiplexer_8_out, multiplexer_4_out);
  or or_4 (or_4_out, multiplexer_4_out, multiplexer_8_out);
  Multiplexer #(.select(2)) multiplexer_9 (
    .in0(and_1_out), .in1(or_1_out), .in2(adder_2_out), .in3(out_17), .out(out_14), .sel(selecao));  // open: en
  Multiplexer #(.select(2)) multiplexer_10 (
    .in0(and_2_out), .in1(or_2_out), .in2(adder_3_out), .in3(in_10), .out(out_15), .sel(selecao));  // open: en
  Multiplexer #(.select(2)) multiplexer_11 (
    .in0(and_3_out), .in1(or_3_out), .in2(adder_4_out), .in3(in_10), .out(out_16), .sel(selecao));  // open: en
  Multiplexer #(.select(2)) multiplexer_12 (
    .in0(and_4_out), .in1(or_4_out), .in2(adder_1_out), .in3(in_10), .out(out_17), .sel(selecao));  // open: en
endmodule
